// Logisim project function.circ as structural Verilog: 1 circuit, main circuit main
module main (
);

  wire and_1_out, and_2_out, and_3_out, and_4_out, and_5_out, and_6_out, and_7_out, and_8_out, and_9_out,
       and_10_out, and_11_out, and_12_out, and_13_out, and_14_out, and_15_out, and_16_out, and_17_out,
       and_18_out, and_19_out, and_20_out, and_21_out, and_22_out, and_23_out, and_24_out, and_25_out,
       and_26_out, and_27_out, and_28_out, and_29_out, and_30_out, and_31_out, and_32_out, and_33_out,
       and_34_out, and_35_out, and_36_out, and_37_out, and_38_out, and_39_out, and_40_out, and_41_out,
       and_42_out, and_43_out, and_44_out, and_45_out, and_46_out, and_47_out, and_48_out, and_49_out,
       and_50_out, and_51_out, and_52_out, and_53_out, and_54_out, and_55_out, and_56_out, and_57_out,
       and_58_out, and_59_out, and_60_out, and_61_out, and_62_out, and_63_out, and_64_out, and_65_out,
       and_66_out, and_67_out, and_68_out, and_69_out, and_70_out, and_71_out, and_72_out, and_73_out,
       and_74_out, and_75_out, and_76_out, and_77_out, and_78_out, and_79_out, and_80_out, and_81_out,
       and_82_out, and_83_out, and_84_out, and_85_out, and_86_out, and_87_out, and_88_out, and_89_out,
       and_90_out, and_91_out, and_92_out, and_93_out, and_94_out, and_95_out, and_96_out, and_97_out,
       and_98_out, and_99_out, and_100_out, button_1_out, button_2_out, button_3_out, button_4_out,
       button_5_out, button_6_out, button_7_out, button_8_out, button_9_out, button_10_out, button_11_out,
       button_12_out, button_13_out, button_14_out, button_15_out, button_16_out, button_17_out,
       button_18_out, button_19_out, button_20_out, button_21_out, button_22_out, button_23_out,
       button_24_out, button_25_out, button_26_out, button_27_out, button_28_out, button_29_out,
       button_30_out, button_31_out, button_32_out, C_out, clock_1_out, d_ff_1_q, d_ff_2_q, d_ff_3_q,
       d_ff_4_q, d_ff_5_q, d_ff_6_q, d_ff_7_q, d_ff_8_q, d_ff_9_q, d_ff_10_q, d_ff_11_q, d_ff_12_q,
       d_ff_13_q, d_ff_14_q, d_ff_15_q, d_ff_16_q, d_ff_17_q, d_ff_18_q, d_ff_19_q, d_ff_20_q, d_ff_21_q,
       d_ff_22_q, d_ff_23_q, d_ff_24_q, d_ff_25_q, d_ff_26_q, d_ff_27_q, d_ff_28_q, d_ff_29_q, d_ff_30_q,
       d_ff_31_q, d_ff_32_q, \L_Л_out , not_1_out, not_2_out, not_3_out, not_4_out, or_1_out, or_2_out,
       or_3_out, or_4_out, or_5_out, or_6_out, or_7_out, or_8_out, or_9_out, or_10_out, or_11_out, or_12_out,
       or_13_out, or_14_out, or_15_out, or_16_out, or_17_out, or_18_out, or_19_out, or_20_out, or_21_out,
       or_22_out, or_23_out, or_24_out, or_25_out, or_26_out, or_27_out, or_28_out, or_29_out, or_30_out,
       or_31_out, or_32_out, \R_Л_out , x_out, \Y_ЗП_out ;

  Clock x (.out(x_out));
  Button C (.out(C_out));
  Clock clock_1 (.out(clock_1_out));
  Button \R_Л  (.out(\R_Л_out ));
  Button button_1 (.out(button_1_out));
  Button \L_Л  (.out(\L_Л_out ));
  Button \Y_ЗП  (.out(\Y_ЗП_out ));
  not not_1 (not_1_out, and_1_out);
  and and_1 (and_1_out, x_out, C_out);
  not not_2 (not_2_out, and_2_out);
  and and_2 (and_2_out, not_1_out, C_out);
  and and_3 (and_3_out, \R_Л_out , 1'b0);
  or or_1 (or_1_out, and_3_out, and_4_out, and_5_out);
  and and_4 (and_4_out, d_ff_2_q, \L_Л_out );
  and and_5 (and_5_out, button_1_out, \Y_ЗП_out );
  D_Flip_Flop d_ff_1 (.clk(clock_1_out), .D(or_1_out), .Q(d_ff_1_q));  // open: Qn, preset, en, reset
  not not_3 (not_3_out, and_6_out);
  and and_6 (and_6_out, not_1_out, not_4_out);
  not not_4 (not_4_out, and_7_out);
  and and_7 (and_7_out, not_3_out, not_2_out);
  Button button_2 (.out(button_2_out));
  LED led_1 (.in(not_3_out));
  LED led_2 (.in(not_4_out));
  and and_8 (and_8_out, \R_Л_out , d_ff_1_q);
  and and_9 (and_9_out, d_ff_3_q, \L_Л_out );
  and and_10 (and_10_out, button_2_out, \Y_ЗП_out );
  D_Flip_Flop d_ff_2 (.clk(clock_1_out), .D(or_2_out), .Q(d_ff_2_q));  // open: Qn, preset, en, reset
  or or_2 (or_2_out, and_8_out, and_9_out, and_10_out);
  Button button_3 (.out(button_3_out));
  and and_11 (and_11_out, \R_Л_out , d_ff_2_q);
  and and_12 (and_12_out, d_ff_4_q, \L_Л_out );
  and and_13 (and_13_out, button_3_out, \Y_ЗП_out );
  or or_3 (or_3_out, and_11_out, and_12_out, and_13_out);
  D_Flip_Flop d_ff_3 (.clk(clock_1_out), .D(or_3_out), .Q(d_ff_3_q));  // open: Qn, preset, en, reset
  Button button_4 (.out(button_4_out));
  and and_14 (and_14_out, \R_Л_out , d_ff_3_q);
  and and_15 (and_15_out, d_ff_5_q, \L_Л_out );
  and and_16 (and_16_out, button_4_out, \Y_ЗП_out );
  or or_4 (or_4_out, and_14_out, and_15_out, and_16_out);
  D_Flip_Flop d_ff_4 (.clk(clock_1_out), .D(or_4_out), .Q(d_ff_4_q));  // open: Qn, preset, en, reset
  Button button_5 (.out(button_5_out));
  and and_17 (and_17_out, \R_Л_out , d_ff_4_q);
  or or_5 (or_5_out, and_17_out, and_18_out, and_19_out);
  and and_18 (and_18_out, d_ff_6_q, \L_Л_out );
  and and_19 (and_19_out, button_5_out, \Y_ЗП_out );
  D_Flip_Flop d_ff_5 (.clk(clock_1_out), .D(or_5_out), .Q(d_ff_5_q));  // open: Qn, preset, en, reset
  Button button_6 (.out(button_6_out));
  and and_20 (and_20_out, \R_Л_out , d_ff_5_q);
  and and_21 (and_21_out, d_ff_7_q, \L_Л_out );
  and and_22 (and_22_out, button_6_out, \Y_ЗП_out );
  D_Flip_Flop d_ff_6 (.clk(clock_1_out), .D(or_6_out), .Q(d_ff_6_q));  // open: Qn, preset, en, reset
  or or_6 (or_6_out, and_20_out, and_21_out, and_22_out);
  Button button_7 (.out(button_7_out));
  and and_23 (and_23_out, \R_Л_out , d_ff_6_q);
  and and_24 (and_24_out, d_ff_8_q, \L_Л_out );
  and and_25 (and_25_out, button_7_out, \Y_ЗП_out );
  or or_7 (or_7_out, and_23_out, and_24_out, and_25_out);
  D_Flip_Flop d_ff_7 (.clk(clock_1_out), .D(or_7_out), .Q(d_ff_7_q));  // open: Qn, preset, en, reset
  Button button_8 (.out(button_8_out));
  and and_26 (and_26_out, \R_Л_out , d_ff_7_q);
  and and_27 (and_27_out, d_ff_9_q, \L_Л_out );
  and and_28 (and_28_out, button_8_out, \Y_ЗП_out );
  or or_8 (or_8_out, and_26_out, and_27_out, and_28_out);
  D_Flip_Flop d_ff_8 (.clk(clock_1_out), .D(or_8_out), .Q(d_ff_8_q));  // open: Qn, preset, en, reset
  Button button_9 (.out(button_9_out));
  and and_29 (and_29_out, \R_Л_out , d_ff_8_q);
  and and_30 (and_30_out, d_ff_10_q, \L_Л_out );
  or or_9 (or_9_out, and_29_out, and_30_out, and_31_out);
  and and_31 (and_31_out, button_9_out, \Y_ЗП_out );
  D_Flip_Flop d_ff_9 (.clk(clock_1_out), .D(or_9_out), .Q(d_ff_9_q));  // open: Qn, preset, en, reset
  Button button_10 (.out(button_10_out));
  and and_32 (and_32_out, \R_Л_out , d_ff_9_q);
  and and_33 (and_33_out, d_ff_11_q, \L_Л_out );
  and and_34 (and_34_out, button_10_out, \Y_ЗП_out );
  D_Flip_Flop d_ff_10 (.clk(clock_1_out), .D(or_10_out), .Q(d_ff_10_q));  // open: Qn, preset, en, reset
  or or_10 (or_10_out, and_32_out, and_33_out, and_34_out);
  Button button_11 (.out(button_11_out));
  and and_35 (and_35_out, \R_Л_out , d_ff_10_q);
  and and_36 (and_36_out, d_ff_12_q, \L_Л_out );
  and and_37 (and_37_out, button_11_out, \Y_ЗП_out );
  or or_11 (or_11_out, and_35_out, and_36_out, and_37_out);
  D_Flip_Flop d_ff_11 (.clk(clock_1_out), .D(or_11_out), .Q(d_ff_11_q));  // open: Qn, preset, en, reset
  Button button_12 (.out(button_12_out));
  and and_38 (and_38_out, \R_Л_out , d_ff_11_q);
  and and_39 (and_39_out, d_ff_13_q, \L_Л_out );
  and and_40 (and_40_out, button_12_out, \Y_ЗП_out );
  or or_12 (or_12_out, and_38_out, and_39_out, and_40_out);
  D_Flip_Flop d_ff_12 (.clk(clock_1_out), .D(or_12_out), .Q(d_ff_12_q));  // open: Qn, preset, en, reset
  Button button_13 (.out(button_13_out));
  and and_41 (and_41_out, \R_Л_out , d_ff_12_q);
  or or_13 (or_13_out, and_41_out, and_42_out, and_43_out);
  and and_42 (and_42_out, d_ff_14_q, \L_Л_out );
  and and_43 (and_43_out, button_13_out, \Y_ЗП_out );
  D_Flip_Flop d_ff_13 (.clk(clock_1_out), .D(or_13_out), .Q(d_ff_13_q));  // open: Qn, preset, en, reset
  Button button_14 (.out(button_14_out));
  and and_44 (and_44_out, \R_Л_out , d_ff_13_q);
  and and_45 (and_45_out, d_ff_15_q, \L_Л_out );
  and and_46 (and_46_out, button_14_out, \Y_ЗП_out );
  D_Flip_Flop d_ff_14 (.clk(clock_1_out), .D(or_14_out), .Q(d_ff_14_q));  // open: Qn, preset, en, reset
  or or_14 (or_14_out, and_44_out, and_45_out, and_46_out);
  Button button_15 (.out(button_15_out));
  and and_47 (and_47_out, \R_Л_out , d_ff_14_q);
  and and_48 (and_48_out, d_ff_16_q, \L_Л_out );
  and and_49 (and_49_out, button_15_out, \Y_ЗП_out );
  or or_15 (or_15_out, and_47_out, and_48_out, and_49_out);
  D_Flip_Flop d_ff_15 (.clk(clock_1_out), .D(or_15_out), .Q(d_ff_15_q));  // open: Qn, preset, en, reset
  Button button_16 (.out(button_16_out));
  and and_50 (and_50_out, \R_Л_out , d_ff_15_q);
  and and_51 (and_51_out, d_ff_17_q, \L_Л_out );
  and and_52 (and_52_out, button_16_out, \Y_ЗП_out );
  or or_16 (or_16_out, and_50_out, and_51_out, and_52_out);
  D_Flip_Flop d_ff_16 (.clk(clock_1_out), .D(or_16_out), .Q(d_ff_16_q));  // open: Qn, preset, en, reset
  Button button_17 (.out(button_17_out));
  and and_53 (and_53_out, \R_Л_out , d_ff_16_q);
  or or_17 (or_17_out, and_53_out, and_54_out, and_55_out);
  and and_54 (and_54_out, d_ff_18_q, \L_Л_out );
  and and_55 (and_55_out, button_17_out, \Y_ЗП_out );
  D_Flip_Flop d_ff_17 (.clk(clock_1_out), .D(or_17_out), .Q(d_ff_17_q));  // open: Qn, preset, en, reset
  Button button_18 (.out(button_18_out));
  and and_56 (and_56_out, \R_Л_out , d_ff_17_q);
  and and_57 (and_57_out, d_ff_19_q, \L_Л_out );
  and and_58 (and_58_out, button_18_out, \Y_ЗП_out );
  D_Flip_Flop d_ff_18 (.clk(clock_1_out), .D(or_18_out), .Q(d_ff_18_q));  // open: Qn, preset, en, reset
  or or_18 (or_18_out, and_56_out, and_57_out, and_58_out);
  Button button_19 (.out(button_19_out));
  and and_59 (and_59_out, \R_Л_out , d_ff_18_q);
  and and_60 (and_60_out, d_ff_20_q, \L_Л_out );
  and and_61 (and_61_out, button_19_out, \Y_ЗП_out );
  or or_19 (or_19_out, and_59_out, and_60_out, and_61_out);
  D_Flip_Flop d_ff_19 (.clk(clock_1_out), .D(or_19_out), .Q(d_ff_19_q));  // open: Qn, preset, en, reset
  Button button_20 (.out(button_20_out));
  and and_62 (and_62_out, \R_Л_out , d_ff_19_q);
  and and_63 (and_63_out, d_ff_21_q, \L_Л_out );
  and and_64 (and_64_out, button_20_out, \Y_ЗП_out );
  or or_20 (or_20_out, and_62_out, and_63_out, and_64_out);
  D_Flip_Flop d_ff_20 (.clk(clock_1_out), .D(or_20_out), .Q(d_ff_20_q));  // open: Qn, preset, en, reset
  Button button_21 (.out(button_21_out));
  and and_65 (and_65_out, \R_Л_out , d_ff_20_q);
  or or_21 (or_21_out, and_65_out, and_66_out, and_67_out);
  and and_66 (and_66_out, d_ff_22_q, \L_Л_out );
  and and_67 (and_67_out, button_21_out, \Y_ЗП_out );
  D_Flip_Flop d_ff_21 (.clk(clock_1_out), .D(or_21_out), .Q(d_ff_21_q));  // open: Qn, preset, en, reset
  Button button_22 (.out(button_22_out));
  and and_68 (and_68_out, \R_Л_out , d_ff_21_q);
  and and_69 (and_69_out, d_ff_23_q, \L_Л_out );
  and and_70 (and_70_out, button_22_out, \Y_ЗП_out );
  D_Flip_Flop d_ff_22 (.clk(clock_1_out), .D(or_22_out), .Q(d_ff_22_q));  // open: Qn, preset, en, reset
  or or_22 (or_22_out, and_68_out, and_69_out, and_70_out);
  Button button_23 (.out(button_23_out));
  and and_71 (and_71_out, \R_Л_out , d_ff_22_q);
  and and_72 (and_72_out, d_ff_24_q, \L_Л_out );
  and and_73 (and_73_out, button_23_out, \Y_ЗП_out );
  or or_23 (or_23_out, and_71_out, and_72_out, and_73_out);
  D_Flip_Flop d_ff_23 (.clk(clock_1_out), .D(or_23_out), .Q(d_ff_23_q));  // open: Qn, preset, en, reset
  Button button_24 (.out(button_24_out));
  and and_74 (and_74_out, \R_Л_out , d_ff_23_q);
  and and_75 (and_75_out, d_ff_25_q, \L_Л_out );
  and and_76 (and_76_out, button_24_out, \Y_ЗП_out );
  or or_24 (or_24_out, and_74_out, and_75_out, and_76_out);
  D_Flip_Flop d_ff_24 (.clk(clock_1_out), .D(or_24_out), .Q(d_ff_24_q));  // open: Qn, preset, en, reset
  Button button_25 (.out(button_25_out));
  and and_77 (and_77_out, \R_Л_out , d_ff_24_q);
  and and_78 (and_78_out, d_ff_26_q, \L_Л_out );
  or or_25 (or_25_out, and_77_out, and_78_out, and_79_out);
  and and_79 (and_79_out, button_25_out, \Y_ЗП_out );
  D_Flip_Flop d_ff_25 (.clk(clock_1_out), .D(or_25_out), .Q(d_ff_25_q));  // open: Qn, preset, en, reset
  Button button_26 (.out(button_26_out));
  and and_80 (and_80_out, \R_Л_out , d_ff_25_q);
  and and_81 (and_81_out, d_ff_27_q, \L_Л_out );
  and and_82 (and_82_out, button_26_out, \Y_ЗП_out );
  D_Flip_Flop d_ff_26 (.clk(clock_1_out), .D(or_26_out), .Q(d_ff_26_q));  // open: Qn, preset, en, reset
  or or_26 (or_26_out, and_80_out, and_81_out, and_82_out);
  Button button_27 (.out(button_27_out));
  and and_83 (and_83_out, \R_Л_out , d_ff_26_q);
  and and_84 (and_84_out, d_ff_28_q, \L_Л_out );
  and and_85 (and_85_out, button_27_out, \Y_ЗП_out );
  or or_27 (or_27_out, and_83_out, and_84_out, and_85_out);
  D_Flip_Flop d_ff_27 (.clk(clock_1_out), .D(or_27_out), .Q(d_ff_27_q));  // open: Qn, preset, en, reset
  Button button_28 (.out(button_28_out));
  and and_86 (and_86_out, \R_Л_out , d_ff_27_q);
  and and_87 (and_87_out, d_ff_29_q, \L_Л_out );
  and and_88 (and_88_out, button_28_out, \Y_ЗП_out );
  or or_28 (or_28_out, and_86_out, and_87_out, and_88_out);
  D_Flip_Flop d_ff_28 (.clk(clock_1_out), .D(or_28_out), .Q(d_ff_28_q));  // open: Qn, preset, en, reset
  Button button_29 (.out(button_29_out));
  and and_89 (and_89_out, \R_Л_out , d_ff_28_q);
  and and_90 (and_90_out, d_ff_30_q, \L_Л_out );
  or or_29 (or_29_out, and_89_out, and_90_out, and_91_out);
  and and_91 (and_91_out, button_29_out, \Y_ЗП_out );
  D_Flip_Flop d_ff_29 (.clk(clock_1_out), .D(or_29_out), .Q(d_ff_29_q));  // open: Qn, preset, en, reset
  Button button_30 (.out(button_30_out));
  and and_92 (and_92_out, \R_Л_out , d_ff_29_q);
  and and_93 (and_93_out, d_ff_31_q, \L_Л_out );
  and and_94 (and_94_out, button_30_out, \Y_ЗП_out );
  D_Flip_Flop d_ff_30 (.clk(clock_1_out), .D(or_30_out), .Q(d_ff_30_q));  // open: Qn, preset, en, reset
  or or_30 (or_30_out, and_92_out, and_93_out, and_94_out);
  Button button_31 (.out(button_31_out));
  and and_95 (and_95_out, \R_Л_out , d_ff_30_q);
  and and_96 (and_96_out, d_ff_32_q, \L_Л_out );
  and and_97 (and_97_out, button_31_out, \Y_ЗП_out );
  or or_31 (or_31_out, and_95_out, and_96_out, and_97_out);
  D_Flip_Flop d_ff_31 (.clk(clock_1_out), .D(or_31_out), .Q(d_ff_31_q));  // open: Qn, preset, en, reset
  Button button_32 (.out(button_32_out));
  and and_98 (and_98_out, \R_Л_out , d_ff_31_q);
  and and_99 (and_99_out, 1'b0, \L_Л_out );
  and and_100 (and_100_out, button_32_out, \Y_ЗП_out );
  or or_32 (or_32_out, and_98_out, and_99_out, and_100_out);
  D_Flip_Flop d_ff_32 (.clk(clock_1_out), .D(or_32_out), .Q(d_ff_32_q));  // open: Qn, preset, en, reset
endmodule
